# Fritzing sketch TecladoNFP-Ligação dos fios (saved by Fritzing 1.0.1rc)

parts:
  Part1 = Bluetooth HC-05 Macho
  Part2 = Arduino Micro (Rev3)

nets:
  N1: Part1.TXD, Part2.D9_PWM/A9
  N2: Part1.RXD, Part2.D8_PWM/A8
  VCC: Part1.VCC, Part2.5V
  GND: Part1.GND, Part2.GND
